// Logisim project rock_paper.circ as structural Verilog: 1 circuit, main circuit main
module main (
);

  wire and_1_out, and_2_out, and_3_out, and_4_out, and_5_out, and_6_out, and_7_out, and_8_out, and_9_out,
       and_10_out, and_11_out, and_12_out, and_13_out, and_14_out, and_15_out, dipswitch_1_p1,
       dipswitch_1_p2, dipswitch_2_p1, dipswitch_2_p2, not_1_out, not_2_out, not_3_out, not_4_out, or_1_out,
       or_2_out, or_3_out;

  // DipSwitch #(.number(2)) dipswitch_1: pin names not known; wires that end beside it: dipswitch_1_p1, dipswitch_1_p2
  // DipSwitch #(.number(2)) dipswitch_2: pin names not known; wires that end beside it: dipswitch_2_p1, dipswitch_2_p2
  and and_1 (and_1_out, dipswitch_1_p2, not_1_out);
  not not_1 (not_1_out, dipswitch_1_p1);
  and and_2 (and_2_out, dipswitch_1_p2, dipswitch_1_p1);
  not not_2 (not_2_out, dipswitch_1_p2);
  and and_3 (and_3_out, not_2_out, dipswitch_1_p1);
  and and_4 (and_4_out, dipswitch_2_p2, not_3_out);
  not not_3 (not_3_out, dipswitch_2_p1);
  and and_5 (and_5_out, dipswitch_2_p2, dipswitch_2_p1);
  not not_4 (not_4_out, dipswitch_2_p2);
  and and_6 (and_6_out, not_4_out, dipswitch_2_p1);
  and and_7 (and_7_out, and_1_out, and_4_out);
  and and_8 (and_8_out, and_2_out, and_5_out);
  and and_9 (and_9_out, and_3_out, and_6_out);
  and and_10 (and_10_out, and_1_out, and_6_out);
  and and_11 (and_11_out, and_1_out, and_5_out);
  and and_12 (and_12_out, and_3_out, and_5_out);
  or or_1 (or_1_out, and_7_out, and_8_out, and_9_out);
  LED led_1 (.in(or_1_out));
  and and_13 (and_13_out, and_4_out, and_2_out);
  and and_14 (and_14_out, and_5_out, and_3_out);
  and and_15 (and_15_out, and_2_out, and_6_out);
  or or_2 (or_2_out, and_10_out, and_11_out, and_12_out);
  LED led_2 (.in(or_2_out));
  or or_3 (or_3_out, and_13_out, and_14_out, and_15_out);
  LED led_3 (.in(or_3_out));

  // Notes on the sheet:
  //   Player B
  //   Player A
  //   Ra
  //   Pa
  //   Sa
  //   Rb
  //   Pb
  //   Sb
  //   TIE
  //   A
  //   Code
  //   01->Rock
  //   11->Paper
  //   10->Scissor
  //   B
endmodule
